// Logisim project cpu.circ as structural Verilog: 13 circuits, main circuit main
module main (
);

  wire A_IN, A_OUT, AB_SEL0, AB_SEL1, AB_SEL2, adder_1_cout, ADDR_ABUS_OUT, ADDR_INH, ADDR_INL, ALU_ADD,
       ALU_AND, ALU_C, ALU_NONE, ALU_OR, ALU_OUT, ALU_RSH, ALU_SEL0, ALU_SEL1, ALU_SEL2, ALU_SUB, ALU_XOR,
       and_1_out, and_2_out, and_3_out, and_4_out, and_5_out, and_6_out, and_7_out, and_8_out, and_9_out,
       and_10_out, and_11_out, and_12_out, and_13_out, and_17_out, and_18_out, and_19_out, and_20_out,
       and_21_out, and_22_out, B_IN, B_OUT, C, C_IN, C_JMP, C_OUT, CIE, CLK, comparator_1_eq, d_ff_1_q, D_IN,
       D_OUT, DB_SEL0, DB_SEL1, DB_SEL2, DB_SEL3, DB_SEL4, DB_TAR_SEL0, DB_TAR_SEL1, DB_TAR_SEL2,
       DB_TAR_SEL3, DB_TAR_SEL4, decoder_1_out0, decoder_1_out2, decoder_1_out3, decoder_1_out4,
       decoder_1_out5, decoder_1_out6, decoder_1_out7, decoder_2_out0, decoder_2_out1, decoder_2_out2,
       decoder_2_out3, decoder_2_out4, decoder_2_out5, decoder_2_out6, decoder_2_out7, decoder_5_out21,
       decoder_6_out0, decoder_6_out1, decoder_6_out2, decoder_6_out3, decoder_7_out0, decoder_7_out1,
       decoder_7_out2, decoder_7_out3, decoder_8_out13, decoder_8_out14, decoder_8_out19, decoder_9_out0,
       decoder_9_out1, decoder_9_out2, decoder_9_out3, decoder_9_out4, decoder_9_out5, decoder_9_out6,
       decoder_9_out7, DISP2_IN, DISP_IN, E_IN, E_OUT, F_IN, F_OUT, FLAG_INV, FLAGS_IN, FLAGS_OUT, G_IN,
       G_OUT, H_IN, H_OUT, HALT, IDX_ABUS_OUT, IDX_IN, IDX_INH, IDX_INL, IDX_OUTH, IDX_OUTL, INSB_HI,
       INSB_HO, INSB_O, IO_OUT, IR2_IN, IR_IN, IRQ, IRQ_ABUS_OUT, JMP, MEM_OUT, MISC_SEL0, MISC_SEL1,
       MISC_SEL2, MODE_2_out, MODE_out, N, N_JMP, not_3_out, not_4_out, not_5_out, not_6_out, not_7_out,
       not_8_out, not_9_out, not_10_out, not_11_out, not_13_out, not_14_out, not_15_out, O, O_JMP,
       OFF_ABUS_OUT, OFF_ABUS_OUT2, OFF_INH, OFF_INL, OFF_OUTH, OFF_OUTL, OP_IN, or_1_out, or_2_out,
       or_3_out, or_4_out, or_5_out, or_6_out, or_7_out, or_8_out, or_9_out, or_13_out, or_14_out, or_15_out,
       OSC_out, PC_ABUS_OUT, PC_IN, PC_OUTH, PC_OUTL, PORTA_IN, PORTB_IN, RAM_IN, RESET, RUN, RUN_STOP_out,
       SIE, SP_ABUS_OUT, SP_DEC, SP_INC, STEP_out, t_ff_1_q, T_ONE, T_RESET, T_RESET_PF, xnor_1_out,
       xor_1_out, xor_2_out, xor_3_out, xor_4_out, xor_5_out, xor_8_out, xor_9_out, Z, Z_JMP;
  wire [0:0] _4x28C16_data_2;
  wire [1:0] MODE, MODE2, pull_resistor_1_node, rom_2_p1, rom_3_p1;
  wire [2:0] and_15_out, T_STATE;
  wire [3:0] multiplexer_3_out, multiplexer_4_out, undriven, undriven_3, undriven_5, undriven_7, undriven_9,
       undriven_11, undriven_13, undriven_15;
  wire [5:0] U_out;
  wire [7:0] _4x28C16_data, adder_1_out, and_16_out, controlled_buffer_23_out, counter_6_q, counter_6_q_2,
       counter_9_q, IR_REG, IR_REG2, not_25_out, not_25_out_2, OP_REG, or_12_out, register_1_q, register_2_q,
       register_2_q_2, register_6_q, register_7_q, register_8_q, register_9_q, register_10_q, register_11_q,
       register_12_q, register_13_q, register_14_q, register_20_q, register_21_q, register_22_q,
       register_23_q, register_24_q, register_25_q, register_26_q, register_27_q, register_28_q,
       register_29_q, rom_1_data, W_BUS, W_BUS2, xor_6_out, xor_7_out;
  wire [7:4] undriven_2, undriven_4, undriven_6, undriven_8, undriven_10, undriven_12, undriven_14,
       undriven_16;
  wire [7:7] and_14_out;
  wire [14:0] controlled_buffer_31_out, counter_5_q, not_12_out, register_19_q;
  wire [15:0] AD_BUS, controlled_buffer_3_out, controlled_buffer_36_out, counter_1_q, not_24_out,
       subtractor_1_out;
  wire [15:15] not_1_out, not_2_out;
  wire [31:0] counter_2_q, counter_3_q;

  LED Df (.in(register_2_q[7]));
  LED Df_2 (.in(AD_BUS[15]));
  Button L (.out(U_out[1]));
  LED De (.in(register_2_q[6]));
  LED Dd (.in(register_2_q[5]));
  LED Dc (.in(register_2_q[4]));
  LED Db (.in(register_2_q[3]));
  assign AD_BUS = ADDR_ABUS_OUT ? {register_2_q, register_2_q_2} : 16'bz;  // Controlled_Buffer controlled_buffer_1
  LED De_2 (.in(AD_BUS[14]));
  LED Dd_2 (.in(AD_BUS[13]));
  LED Dc_2 (.in(AD_BUS[12]));
  LED Db_2 (.in(AD_BUS[11]));
  // Buffer buffer_1 is placed but not wired
  Button U (.out(U_out[0]));
  Button R (.out(U_out[2]));
  Button D (.out(U_out[5]));
  LED Da (.in(register_2_q[2]));
  LED D9 (.in(register_2_q[1]));
  LED D8 (.in(register_2_q[0]));
  LED Da_2 (.in(AD_BUS[10]));
  LED D9_2 (.in(AD_BUS[9]));
  LED D8_2 (.in(AD_BUS[8]));
  LED D7 (.in(AD_BUS[7]));
  assign AD_BUS = IRQ_ABUS_OUT ? 16'hfff8 : 16'bz;  // Controlled_Buffer controlled_buffer_2
  Button B (.out(U_out[3]));
  Button A (.out(U_out[4]));
  LED D7_2 (.in(register_2_q_2[7]));
  LED D6 (.in(register_2_q_2[6]));
  LED D5 (.in(register_2_q_2[5]));
  LED D4 (.in(register_2_q_2[4]));
  assign controlled_buffer_3_out = ADDR_INL ? {register_2_q, W_BUS} : 16'bz;  // Controlled_Buffer controlled_buffer_3
  assign controlled_buffer_3_out = ADDR_INH ? {W_BUS, register_2_q_2} : 16'bz;  // Controlled_Buffer controlled_buffer_4
  LED D6_2 (.in(AD_BUS[6]));
  LED D5_2 (.in(AD_BUS[5]));
  LED D4_2 (.in(AD_BUS[4]));
  LED D3 (.in(AD_BUS[3]));
  LED D7_3 (.in(W_BUS[7]));
  LED D6_3 (.in(W_BUS[6]));
  assign W_BUS = FLAGS_OUT ? {4'b0000, N, O, Z, C} : 8'bz;  // Controlled_Buffer controlled_buffer_5
  or or_1 (or_1_out, U_out[0], U_out[5], U_out[4], U_out[3], U_out[2], U_out[1]);
  LED D3_2 (.in(register_2_q_2[3]));
  LED D2 (.in(register_2_q_2[2]));
  LED D1 (.in(register_2_q_2[1]));
  LED D0 (.in(register_2_q_2[0]));
  or or_2 (or_2_out, ADDR_INH, ADDR_INL);
  LED D2_2 (.in(AD_BUS[2]));
  LED D1_2 (.in(AD_BUS[1]));
  LED D0_2 (.in(AD_BUS[0]));
  LED D5_3 (.in(W_BUS[5]));
  LED D4_3 (.in(W_BUS[4]));
  LED D3_3 (.in(W_BUS[3]));
  LED D2_3 (.in(W_BUS[2]));
  assign W_BUS2 = IRQ ? 8'h7f : 8'bz;  // Controlled_Buffer controlled_buffer_6
  assign W_BUS = IO_OUT ? register_1_q : 8'bz;  // Controlled_Buffer controlled_buffer_7
  Register register_1 (.D({2'b00, U_out}), .Q(register_1_q), .clk(or_1_out));  // open: en, clr
  Register #(.width(16)) register_2 (
    .D(controlled_buffer_3_out), .en(or_2_out), .Q({register_2_q, register_2_q_2}), .clk(CLK));  // open: clr
  LED D1_3 (.in(W_BUS[1]));
  LED D0_3 (.in(W_BUS[0]));
  T_Flip_Flop #(.enable("true")) t_ff_1 (
    .clk(or_1_out), .T(1'b1), .Q(t_ff_1_q), .reset(or_3_out), .en(1'b1));  // open: Qn, preset
  or or_3 (or_3_out, and_3_out, RESET);
  D_Flip_Flop d_ff_1 (.D(1'b1), .Q(d_ff_1_q), .preset(SIE), .reset(or_4_out));  // open: clk, Qn
  or or_4 (or_4_out, CIE, RESET);
  not not_1 (not_1_out[15], AD_BUS[15]);
  and and_1 (and_1_out, PC_ABUS_OUT, ~IRQ);  // AND_Gate
  Button u_RESET (.out(RESET));
  Button RUN_STOP (.out(RUN_STOP_out));
  ROM #(.addrWidth(15)) rom_1 (.addr(AD_BUS[14:0]), .data(rom_1_data));
  and and_2 (and_2_out, IR_IN, t_ff_1_q, d_ff_1_q);
  and and_3 (and_3_out, IRQ, T_ONE);
  LED D7_4 (.in(not_2_out[15]));
  LED D6_4 (.in(counter_1_q[14]));
  assign AD_BUS = PC_ABUS_OUT ? {not_2_out[15], counter_1_q[14:0]} : 16'bz;  // Controlled_Buffer controlled_buffer_8
  Counter #(.max('hffff), .width(16)) counter_1 (
    .load(JMP), .D({not_1_out[15], AD_BUS[14:0]}), .count(and_1_out), .Q(counter_1_q), .clk(CLK), .clr(RESET));  // open: carry
  T_Flip_Flop #(.enable("true")) t_ff_2 (
    .clk(RUN_STOP_out), .T(1'b1), .Q(RUN), .reset(RESET), .en(1'b1));  // open: Qn, preset
  xor xor_1 (xor_1_out, C, FLAG_INV);
  xor xor_2 (xor_2_out, Z, FLAG_INV);
  xor xor_3 (xor_3_out, O, FLAG_INV);
  xor xor_4 (xor_4_out, N, FLAG_INV);
  and and_4 (and_4_out, MEM_OUT, ~AD_BUS[15]);  // AND_Gate
  RAM #(.addrWidth(15), .databus("bidir")) ram_1 (.addr(AD_BUS[14:0]), .data(W_BUS));  // open: we, oe, clk
  D_Flip_Flop d_ff_2 (.D(and_2_out), .Q(IRQ), .preset(and_2_out), .reset(or_5_out));  // open: clk, Qn
  or or_5 (or_5_out, T_ONE, RESET);
  LED D5_4 (.in(counter_1_q[13]));
  LED D4_4 (.in(counter_1_q[12]));
  LED D3_4 (.in(counter_1_q[11]));
  LED D2_4 (.in(counter_1_q[10]));
  not not_2 (not_2_out[15], counter_1_q[15]);
  Button STEP (.out(STEP_out));
  Clock OSC (.out(OSC_out));
  LED D1_4 (.in(counter_1_q[9]));
  LED D0_4 (.in(counter_1_q[8]));
  LED D7_5 (.in(counter_1_q[7]));
  Counter #(.max('hffffffff), .width(32)) counter_2 (
    .count(CLK), .Q(counter_2_q), .clk(CLK), .clr(RESET));  // open: load, D, carry
  and and_5 (and_5_out, STEP_out, ~RUN);  // AND_Gate
  and and_6 (and_6_out, RUN, OSC_out);
  or or_6 (or_6_out, HALT, 1'b0);
  or or_7 (or_7_out, PC_IN, and_7_out);
  and and_7 (and_7_out, C_JMP, xor_1_out);
  and and_8 (and_8_out, Z_JMP, xor_2_out);
  and and_9 (and_9_out, O_JMP, xor_3_out);
  or or_8 (or_8_out, and_9_out, and_10_out);
  and and_10 (and_10_out, N_JMP, xor_4_out);
  LED D6_5 (.in(counter_1_q[6]));
  LED D5_5 (.in(counter_1_q[5]));
  LED D4_5 (.in(counter_1_q[4]));
  LED D3_5 (.in(counter_1_q[3]));
  assign W_BUS = PC_OUTH ? counter_1_q[7:0] : 8'bz;  // Controlled_Buffer controlled_buffer_9
  assign W_BUS = PC_OUTL ? {not_2_out[15], counter_1_q[14:8]} : 8'bz;  // Controlled_Buffer controlled_buffer_10
  Counter #(.max('hffffffff), .width(32)) counter_3 (.Q(counter_3_q));  // open: load, D, count, carry, clk, clr
  and and_11 (and_11_out, and_6_out, ~or_6_out);  // AND_Gate
  or or_9 (or_9_out, and_8_out, or_8_out);
  and and_12 (and_12_out, ~IRQ, AD_BUS[15], MEM_OUT);  // AND_Gate
  assign W_BUS = and_12_out ? rom_1_data : 8'bz;  // Controlled_Buffer controlled_buffer_11
  and and_13 (and_13_out, ~IRQ, AD_BUS[15], IR_IN);  // AND_Gate
  assign W_BUS2 = and_13_out ? rom_1_data : 8'bz;  // Controlled_Buffer controlled_buffer_12
  LED D0_5 (.in(counter_1_q[0]));
  LED D2_5 (.in(counter_1_q[2]));
  LED D1_5 (.in(counter_1_q[1]));
  Comparator #(.width(32)) comparator_1 (.a(counter_2_q), .b(counter_3_q), .eq(comparator_1_eq));  // open: gt, lt
  or or_10 (CLK, and_5_out, and_11_out);
  or or_11 (JMP, or_7_out, or_9_out);
  Pull_Resistor pull_resistor_1 (.node(pull_resistor_1_node));
  assign W_BUS = A_OUT ? register_6_q : 8'bz;  // Controlled_Buffer controlled_buffer_13
  assign W_BUS = B_OUT ? register_7_q : 8'bz;  // Controlled_Buffer controlled_buffer_14
  assign W_BUS = C_OUT ? register_8_q : 8'bz;  // Controlled_Buffer controlled_buffer_15
  assign W_BUS = D_OUT ? register_9_q : 8'bz;  // Controlled_Buffer controlled_buffer_16
  assign W_BUS = E_OUT ? register_10_q : 8'bz;  // Controlled_Buffer controlled_buffer_17
  assign W_BUS = F_OUT ? register_11_q : 8'bz;  // Controlled_Buffer controlled_buffer_18
  assign W_BUS = G_OUT ? register_12_q : 8'bz;  // Controlled_Buffer controlled_buffer_19
  assign W_BUS = H_OUT ? register_13_q : 8'bz;  // Controlled_Buffer controlled_buffer_20
  Counter #(.max('h7), .width(3)) counter_4 (
    .load(T_RESET), .D({pull_resistor_1_node, T_RESET_PF}), .count(CLK), .Q(T_STATE), .clk(CLK), .clr(RESET));  // open: carry
  Register register_3 (.D(W_BUS2), .en(IR_IN), .Q(IR_REG), .clk(CLK));  // open: clr
  Register register_4 (.D(W_BUS), .en(IR2_IN), .Q(IR_REG2), .clk(CLK));  // open: clr
  Register register_5 (.D(W_BUS), .en(OP_IN), .Q(OP_REG), .clk(CLK));  // open: clr
  Register register_6 (.D(W_BUS), .en(A_IN), .Q(register_6_q), .clk(CLK));  // open: clr
  Register register_7 (.D(W_BUS), .en(B_IN), .Q(register_7_q), .clk(CLK));  // open: clr
  Register register_8 (.D(W_BUS), .en(C_IN), .Q(register_8_q), .clk(CLK));  // open: clr
  Register register_9 (.D(W_BUS), .en(D_IN), .Q(register_9_q), .clk(CLK));  // open: clr
  Register register_10 (.D(W_BUS), .en(E_IN), .Q(register_10_q), .clk(CLK));  // open: clr
  Register register_11 (.D(W_BUS), .en(F_IN), .Q(register_11_q), .clk(CLK));  // open: clr
  Register register_12 (.D(W_BUS), .en(G_IN), .Q(register_12_q), .clk(CLK));  // open: clr
  Register register_13 (.D(W_BUS), .en(H_IN), .Q(register_13_q), .clk(CLK));  // open: clr
  LED T0 (.in(decoder_1_out0));
  LED T1 (.in(T_ONE));
  LED T2 (.in(decoder_1_out2));
  LED T3 (.in(decoder_1_out3));
  Decoder #(.select(3)) decoder_1 (
    .out0(decoder_1_out0), .out1(T_ONE), .out2(decoder_1_out2), .out3(decoder_1_out3), .out4(decoder_1_out4),
    .out5(decoder_1_out5), .out6(decoder_1_out6), .out7(decoder_1_out7), .sel(T_STATE));  // open: en
  LED D7_6 (.in(IR_REG[7]));
  LED D6_6 (.in(IR_REG[6]));
  LED D5_6 (.in(IR_REG[5]));
  LED D4_6 (.in(IR_REG[4]));
  LED D7_7 (.in(IR_REG2[7]));
  LED D6_7 (.in(IR_REG2[6]));
  LED D5_7 (.in(IR_REG2[5]));
  LED D4_7 (.in(IR_REG2[4]));
  LED D7_8 (.in(OP_REG[7]));
  LED D6_8 (.in(OP_REG[6]));
  LED D5_8 (.in(OP_REG[5]));
  LED D4_8 (.in(OP_REG[4]));
  LED D7_9 (.in(register_6_q[7]));
  LED D6_9 (.in(register_6_q[6]));
  LED D5_9 (.in(register_6_q[5]));
  LED D4_9 (.in(register_6_q[4]));
  LED D7_10 (.in(register_7_q[7]));
  LED D6_10 (.in(register_7_q[6]));
  LED D5_10 (.in(register_7_q[5]));
  LED D4_10 (.in(register_7_q[4]));
  LED D7_11 (.in(register_8_q[7]));
  LED D6_11 (.in(register_8_q[6]));
  LED D5_11 (.in(register_8_q[5]));
  LED D4_11 (.in(register_8_q[4]));
  LED D7_12 (.in(register_9_q[7]));
  LED D6_12 (.in(register_9_q[6]));
  LED D5_12 (.in(register_9_q[5]));
  LED D4_12 (.in(register_9_q[4]));
  LED D7_13 (.in(register_10_q[7]));
  LED D6_13 (.in(register_10_q[6]));
  LED D5_13 (.in(register_10_q[5]));
  LED D4_13 (.in(register_10_q[4]));
  LED D7_14 (.in(register_11_q[7]));
  LED D6_14 (.in(register_11_q[6]));
  LED D5_14 (.in(register_11_q[5]));
  LED D4_14 (.in(register_11_q[4]));
  LED D7_15 (.in(register_12_q[7]));
  LED D6_15 (.in(register_12_q[6]));
  LED D5_15 (.in(register_12_q[5]));
  LED D4_15 (.in(register_12_q[4]));
  LED D7_16 (.in(register_13_q[7]));
  LED D6_16 (.in(register_13_q[6]));
  LED D5_16 (.in(register_13_q[5]));
  LED D4_16 (.in(register_13_q[4]));
  LED T4 (.in(decoder_1_out4));
  LED T5 (.in(decoder_1_out5));
  LED T6 (.in(decoder_1_out6));
  LED T7 (.in(decoder_1_out7));
  LED D3_6 (.in(IR_REG[3]));
  LED D2_6 (.in(IR_REG[2]));
  LED D1_6 (.in(IR_REG[1]));
  LED D0_6 (.in(IR_REG[0]));
  LED D3_7 (.in(IR_REG2[3]));
  LED D2_7 (.in(IR_REG2[2]));
  LED D1_7 (.in(IR_REG2[1]));
  LED D0_7 (.in(IR_REG2[0]));
  LED D3_8 (.in(OP_REG[3]));
  LED D2_8 (.in(OP_REG[2]));
  LED D1_8 (.in(OP_REG[1]));
  LED D0_8 (.in(OP_REG[0]));
  LED D3_9 (.in(register_6_q[3]));
  LED D2_9 (.in(register_6_q[2]));
  LED D1_9 (.in(register_6_q[1]));
  LED D0_9 (.in(register_6_q[0]));
  LED D3_10 (.in(register_7_q[3]));
  LED D2_10 (.in(register_7_q[2]));
  LED D1_10 (.in(register_7_q[1]));
  LED D0_10 (.in(register_7_q[0]));
  LED D3_11 (.in(register_8_q[3]));
  LED D2_11 (.in(register_8_q[2]));
  LED D1_11 (.in(register_8_q[1]));
  LED D0_11 (.in(register_8_q[0]));
  LED D3_12 (.in(register_9_q[3]));
  LED D2_12 (.in(register_9_q[2]));
  LED D1_12 (.in(register_9_q[1]));
  LED D0_12 (.in(register_9_q[0]));
  LED D3_13 (.in(register_10_q[3]));
  LED D2_13 (.in(register_10_q[2]));
  LED D1_13 (.in(register_10_q[1]));
  LED D0_13 (.in(register_10_q[0]));
  LED D3_14 (.in(register_11_q[3]));
  LED D2_14 (.in(register_11_q[2]));
  LED D1_14 (.in(register_11_q[1]));
  LED D0_14 (.in(register_11_q[0]));
  LED D3_15 (.in(register_12_q[3]));
  LED D2_15 (.in(register_12_q[2]));
  LED D1_15 (.in(register_12_q[1]));
  LED D0_15 (.in(register_12_q[0]));
  LED D3_16 (.in(register_13_q[3]));
  LED D2_16 (.in(register_13_q[2]));
  LED D1_16 (.in(register_13_q[1]));
  LED D0_16 (.in(register_13_q[0]));
  and and_14 (and_14_out[7], C, ALU_C);
  LED E (.in(not_12_out[14]));
  assign AD_BUS = SP_ABUS_OUT ? {1'b0, not_12_out} : 16'bz;  // Controlled_Buffer controlled_buffer_21
  assign W_BUS = ALU_OUT ? register_14_q : 8'bz;  // Controlled_Buffer controlled_buffer_22
  Register register_14 (.D(controlled_buffer_23_out), .en(ALU_NONE), .Q(register_14_q), .clk(CLK));  // open: clr
  ROM #(.addrWidth(11), .dataWidth(32)) _4x28C16 (
    .addr({IR_REG, T_STATE}),
    .data({T_RESET_PF, T_RESET, PC_IN, IDX_IN, IR_IN, MISC_SEL2, MISC_SEL1, MISC_SEL0, INSB_HO, INSB_HI, INSB_O, _4x28C16_data_2[0], O_JMP, N_JMP, Z_JMP, C_JMP, ALU_SEL2, ALU_SEL1, ALU_SEL0, DB_SEL4, AB_SEL2, AB_SEL1, AB_SEL0, DB_TAR_SEL4, _4x28C16_data}));
  LED D_2 (.in(not_12_out[13]));
  LED u_C (.in(not_12_out[12]));
  LED B_2 (.in(not_12_out[11]));
  LED A_2 (.in(not_12_out[10]));
  LED D7_17 (.in(register_14_q[7]));
  LED D6_17 (.in(register_14_q[6]));
  LED D5_17 (.in(register_14_q[5]));
  LED D4_17 (.in(register_14_q[4]));
  Register #(.width(1)) register_15 (.D(multiplexer_4_out[2]), .en(not_4_out), .Q(C), .clk(CLK), .clr(RESET));
  and and_15 (and_15_out[0], xnor_1_out, xor_8_out);
  xnor xnor_1 (xnor_1_out, W_BUS[7], xor_6_out[7]);
  xor xor_5 (xor_5_out, and_14_out[7], ALU_ADD);
  assign xor_6_out = OP_REG ^ {8{ALU_ADD}};  // XOR_Gate xor_6, 8 bits wide
  assign xor_7_out = OP_REG ^ W_BUS;  // XOR_Gate xor_7, 8 bits wide
  assign controlled_buffer_23_out = not_8_out ? xor_7_out : 8'bz;  // Controlled_Buffer controlled_buffer_23
  assign and_16_out = OP_REG & W_BUS;  // AND_Gate and_16, 8 bits wide
  assign controlled_buffer_23_out = not_9_out ? and_16_out : 8'bz;  // Controlled_Buffer controlled_buffer_24
  assign or_12_out = OP_REG | W_BUS;  // OR_Gate or_12, 8 bits wide
  assign controlled_buffer_23_out = not_10_out ? or_12_out : 8'bz;  // Controlled_Buffer controlled_buffer_25
  LED _9 (.in(not_12_out[9]));
  LED _8 (.in(not_12_out[8]));
  LED _7 (.in(not_12_out[7]));
  LED _6 (.in(not_12_out[6]));
  not not_3 (not_3_out, SP_INC);
  or or_13 (or_13_out, SP_INC, SP_DEC);
  LED D3_17 (.in(register_14_q[3]));
  LED D2_17 (.in(register_14_q[2]));
  LED D1_17 (.in(register_14_q[1]));
  LED D0_17 (.in(register_14_q[0]));
  Register #(.width(1)) register_16 (.D(multiplexer_4_out[1]), .en(ALU_NONE), .Q(Z), .clk(CLK), .clr(RESET));
  not not_4 (not_4_out, and_17_out);
  and and_17 (and_17_out, and_20_out, ALU_RSH);
  xor xor_8 (xor_8_out, xor_6_out[7], adder_1_out[7]);
  not not_5 (not_5_out, and_20_out);
  assign controlled_buffer_23_out = not_5_out ? adder_1_out : 8'bz;  // Controlled_Buffer controlled_buffer_26
  Adder adder_1 (.a(W_BUS), .b(xor_6_out), .out(adder_1_out), .cin(xor_5_out), .cout(adder_1_cout));
  xor xor_9 (xor_9_out, adder_1_cout, ALU_ADD);
  and and_18 (and_18_out, ALU_NONE, ALU_RSH);
  not not_6 (not_6_out, and_18_out);
  assign controlled_buffer_23_out = not_6_out ? {and_14_out[7], W_BUS[7:1]} : 8'bz;  // Controlled_Buffer controlled_buffer_27
  not not_7 (not_7_out, and_18_out);
  not not_8 (not_8_out, ALU_XOR);
  not not_9 (not_9_out, ALU_AND);
  not not_10 (not_10_out, ALU_OR);
  LED _5 (.in(not_12_out[5]));
  LED _4 (.in(not_12_out[4]));
  LED _3 (.in(not_12_out[3]));
  LED _2 (.in(not_12_out[2]));
  Counter #(.max('h7fff), .width(15)) counter_5 (
    .load(1'b0), .count(or_13_out), .Q(counter_5_q), .up(not_3_out), .clk(CLK), .clr(RESET));  // open: D, carry
  LED C_2 (.in(C));
  LED u_Z (.in(Z));
  LED u_O (.in(O));
  Register #(.width(1)) register_17 (.D(multiplexer_4_out[0]), .en(not_11_out), .Q(O), .clk(CLK), .clr(ALU_NONE));
  not not_11 (not_11_out, and_20_out);
  and and_19 (and_19_out, not_7_out, W_BUS[0]);
  LED _1 (.in(not_12_out[1]));
  LED _0 (.in(not_12_out[0]));
  assign not_12_out = ~counter_5_q;  // NOT_Gate not_12, 15 bits wide
  LED u_N (.in(N));
  Register #(.width(1)) register_18 (.D(multiplexer_4_out[3]), .en(ALU_NONE), .Q(N), .clk(CLK), .clr(RESET));
  and and_20 (and_20_out, ALU_SUB, ALU_ADD);
  Multiplexer #(.enable("false"), .width(4)) multiplexer_1 (
    .in0(_4x28C16_data[3:0]), .in1(IR_REG2[7:4]), .out({DB_TAR_SEL3, DB_TAR_SEL2, DB_TAR_SEL1, DB_TAR_SEL0}),
    .sel(INSB_HI));
  Multiplexer #(.enable("false"), .width(4)) multiplexer_2 (
    .in0(_4x28C16_data[7:4]), .in1(multiplexer_3_out), .out({DB_SEL3, DB_SEL2, DB_SEL1, DB_SEL0}),
    .sel(INSB_O));
  Multiplexer #(.enable("false"), .width(4)) multiplexer_3 (
    .in0(IR_REG2[3:0]), .in1(IR_REG2[7:4]), .out(multiplexer_3_out), .sel(INSB_HO));
  not not_13 (not_13_out, and_20_out);
  and and_21 (and_21_out, not_13_out, xor_9_out);
  not not_14 (not_14_out, and_21_out);
  not not_15 (not_15_out, and_19_out);
  and and_22 (and_22_out, not_14_out, not_15_out);
  not not_16 (and_15_out[2], and_22_out);
  nor nor_1 (and_15_out[1], controlled_buffer_23_out[7], controlled_buffer_23_out[6], controlled_buffer_23_out[5], controlled_buffer_23_out[4], controlled_buffer_23_out[3], controlled_buffer_23_out[2], controlled_buffer_23_out[1], controlled_buffer_23_out[0]);
  Decoder #(.enable("false"), .select(3)) decoder_2 (
    .out0(decoder_2_out0), .out1(decoder_2_out1), .out2(decoder_2_out2), .out3(decoder_2_out3),
    .out4(decoder_2_out4), .out5(decoder_2_out5), .out6(decoder_2_out6), .out7(decoder_2_out7),
    .sel({ALU_SEL2, ALU_SEL1, ALU_SEL0}));
  Decoder #(.enable("false"), .select(3)) decoder_3 (
    .out1(CIE), .out2(SIE), .out3(FLAG_INV), .out4(HALT), .out5(SP_INC), .out6(SP_DEC), .out7(ALU_C),
    .sel({MISC_SEL2, MISC_SEL1, MISC_SEL0}));  // open: out0
  Decoder #(.enable("false"), .select(3)) decoder_4 (
    .out0(ADDR_ABUS_OUT), .out1(SP_ABUS_OUT), .out2(IRQ_ABUS_OUT), .out3(PC_ABUS_OUT), .out4(IDX_ABUS_OUT),
    .out5(OFF_ABUS_OUT), .out6(OFF_ABUS_OUT2), .sel({AB_SEL2, AB_SEL1, AB_SEL0}));  // open: out7
  Multiplexer #(.enable("false"), .width(4)) multiplexer_4 (
    .in0({controlled_buffer_23_out[7], and_15_out}), .in1({W_BUS[3], W_BUS[0], W_BUS[1], W_BUS[2]}),
    .out(multiplexer_4_out), .sel(FLAGS_IN));
  not not_17 (ALU_NONE, decoder_2_out0);
  not not_18 (ALU_ADD, decoder_2_out1);
  not not_19 (ALU_SUB, decoder_2_out2);
  not not_20 (ALU_RSH, decoder_2_out3);
  not not_21 (ALU_XOR, decoder_2_out4);
  not not_22 (ALU_AND, decoder_2_out5);
  not not_23 (ALU_OR, decoder_2_out6);
  LED Df_3 (.in(not_25_out[7]));
  LED De_3 (.in(not_25_out[6]));
  LED Dd_3 (.in(not_25_out[5]));
  LED Dc_3 (.in(not_25_out[4]));
  assign AD_BUS = IDX_ABUS_OUT ? {not_25_out, not_25_out_2} : 16'bz;  // Controlled_Buffer controlled_buffer_28
  assign W_BUS = IDX_OUTH ? not_25_out_2 : 8'bz;  // Controlled_Buffer controlled_buffer_29
  assign W_BUS = IDX_OUTL ? not_25_out : 8'bz;  // Controlled_Buffer controlled_buffer_30
  LED Db_3 (.in(not_25_out[3]));
  LED Da_3 (.in(not_25_out[2]));
  LED D9_3 (.in(not_25_out[1]));
  LED D8_3 (.in(not_25_out[0]));
  LED D7_18 (.in(not_25_out_2[7]));
  LED D6_18 (.in(not_25_out_2[6]));
  LED D5_18 (.in(not_25_out_2[5]));
  LED D4_18 (.in(not_25_out_2[4]));
  LED D3_18 (.in(not_25_out_2[3]));
  LED D2_18 (.in(not_25_out_2[2]));
  LED D1_18 (.in(not_25_out_2[1]));
  assign not_24_out[14:0] = ~controlled_buffer_31_out;  // NOT_Gate not_24, 15 bits wide
  assign {not_24_out[15], controlled_buffer_31_out} = IDX_INL ? {not_25_out, W_BUS} : 16'bz;  // Controlled_Buffer controlled_buffer_31
  assign {not_24_out[15], controlled_buffer_31_out} = IDX_IN ? AD_BUS : 16'bz;  // Controlled_Buffer controlled_buffer_32
  assign {not_24_out[15], controlled_buffer_31_out} = IDX_INH ? {W_BUS, not_25_out_2} : 16'bz;  // Controlled_Buffer controlled_buffer_33
  Pull_Resistor pull_resistor_2 (.node({not_24_out[15], controlled_buffer_31_out}));
  or or_14 (or_14_out, IDX_INH, IDX_IN, IDX_INL);
  LED D0_18 (.in(not_25_out_2[0]));
  assign {not_25_out[6:0], not_25_out_2} = ~register_19_q;  // NOT_Gate not_25, 15 bits wide
  Register #(.width(16)) register_19 (
    .D(not_24_out), .en(or_14_out), .Q({not_25_out[7], register_19_q}), .clk(CLK));  // open: clr
  Decoder #(.enable("false"), .select(5)) decoder_5 (
    .out1(A_IN), .out2(B_IN), .out3(C_IN), .out4(D_IN), .out5(E_IN), .out6(F_IN), .out7(G_IN), .out8(H_IN),
    .out9(OFF_INH), .out10(OFF_INL), .out11(PORTA_IN), .out12(PORTB_IN), .out13(DISP_IN), .out14(DISP2_IN),
    .out15(IR2_IN), .out16(FLAGS_IN), .out17(OP_IN), .out18(IDX_INL), .out19(IDX_INH), .out20(RAM_IN),
    .out21(decoder_5_out21), .out22(ADDR_INH), .out23(ADDR_INL),
    .sel({DB_TAR_SEL4, DB_TAR_SEL3, DB_TAR_SEL2, DB_TAR_SEL1, DB_TAR_SEL0}));  // open: out0, out24, out25, out26, out27, out28, out29, out30, out31
  LED Df_4 (.in(counter_6_q[7]));
  LED De_4 (.in(counter_6_q[6]));
  LED Dd_4 (.in(counter_6_q[5]));
  LED Dc_4 (.in(counter_6_q[4]));
  LED Db_4 (.in(counter_6_q[3]));
  assign AD_BUS = OFF_ABUS_OUT2 ? {counter_6_q, counter_6_q_2} : 16'bz;  // Controlled_Buffer controlled_buffer_34
  Subtractor #(.width(16)) subtractor_1 (
    .a({not_25_out, not_25_out_2}), .b({counter_6_q, counter_6_q_2}), .out(subtractor_1_out));  // open: bin, bout
  assign AD_BUS = OFF_ABUS_OUT ? subtractor_1_out : 16'bz;  // Controlled_Buffer controlled_buffer_35
  LED Da_4 (.in(counter_6_q[2]));
  LED D9_4 (.in(counter_6_q[1]));
  LED D8_4 (.in(counter_6_q[0]));
  LED D7_19 (.in(counter_6_q_2[7]));
  LED D6_19 (.in(counter_6_q_2[6]));
  LED D5_19 (.in(counter_6_q_2[5]));
  LED D4_19 (.in(counter_6_q_2[4]));
  LED D3_19 (.in(counter_6_q_2[3]));
  assign controlled_buffer_36_out = OFF_INL ? {counter_6_q, W_BUS} : 16'bz;  // Controlled_Buffer controlled_buffer_36
  assign controlled_buffer_36_out = OFF_INH ? {W_BUS, counter_6_q_2} : 16'bz;  // Controlled_Buffer controlled_buffer_37
  assign W_BUS = OFF_OUTL ? counter_6_q_2 : 8'bz;  // Controlled_Buffer controlled_buffer_38
  LED D2_19 (.in(counter_6_q_2[2]));
  LED D1_19 (.in(counter_6_q_2[1]));
  LED D0_19 (.in(counter_6_q_2[0]));
  Counter #(.max('hffff), .width(16)) counter_6 (
    .load(or_15_out), .D(controlled_buffer_36_out), .count(1'b0), .Q({counter_6_q, counter_6_q_2}),
    .up(1'b0), .clk(CLK));  // open: carry, clr
  or or_15 (or_15_out, OFF_INH, OFF_INL);
  assign W_BUS = OFF_OUTH ? counter_6_q : 8'bz;  // Controlled_Buffer controlled_buffer_39
  Counter #(.max('h3), .width(2)) counter_7 (.D(rom_2_p1), .Q(MODE), .clk(MODE_out));  // open: load, count, carry, clr
  LED UNSINGED (.in(decoder_6_out0));
  LED SIGNED (.in(decoder_6_out1));
  Decoder #(.select(2)) decoder_6 (
    .out0(decoder_6_out0), .out1(decoder_6_out1), .out2(decoder_6_out2), .out3(decoder_6_out3), .sel(MODE));  // open: en
  LED HEX (.in(decoder_6_out2));
  LED OCTAL (.in(decoder_6_out3));
  Decoder #(.select(2)) decoder_7 (
    .out0(decoder_7_out0), .out1(decoder_7_out1), .out2(decoder_7_out2), .out3(decoder_7_out3), .sel(MODE2));  // open: en
  Decoder #(.enable("false"), .select(5)) decoder_8 (
    .out0(MEM_OUT), .out1(A_OUT), .out2(B_OUT), .out3(C_OUT), .out4(D_OUT), .out5(E_OUT), .out6(F_OUT),
    .out7(G_OUT), .out8(H_OUT), .out9(OFF_OUTH), .out10(OFF_OUTL), .out11(ALU_OUT), .out12(FLAGS_OUT),
    .out13(decoder_8_out13), .out14(decoder_8_out14), .out15(PC_OUTL), .out16(PC_OUTH), .out17(IDX_OUTL),
    .out18(IDX_OUTH), .out19(decoder_8_out19), .out20(IO_OUT),
    .sel({DB_SEL4, DB_SEL3, DB_SEL2, DB_SEL1, DB_SEL0}));  // open: out21, out22, out23, out24, out25, out26, out27, out28, out29, out30, out31
  Register register_20 (.D(W_BUS), .en(DISP2_IN), .Q(register_20_q), .clk(CLK));  // open: clr
  Button u_MODE (.out(MODE_out));
  Counter #(.max('h3), .width(2)) counter_8 (
    .D(rom_3_p1), .Q(MODE2), .clk(MODE_2_out));  // open: load, count, carry, clr
  Register register_21 (.D(W_BUS), .en(DISP_IN), .Q(register_21_q), .clk(CLK), .clr(RESET));
  Button MODE_2 (.out(MODE_2_out));
  LED UNSINGED_2 (.in(decoder_7_out0));
  LED SIGNED_2 (.in(decoder_7_out1));
  LED HEX_2 (.in(decoder_7_out2));
  LED OCTAL_2 (.in(decoder_7_out3));
  Counter counter_9 (.load(PORTA_IN), .D(W_BUS), .count(PORTA_IN), .Q(counter_9_q), .clk(CLK));  // open: carry, clr
  // ROM #(.addrWidth(10), .dataWidth(32)) rom_2: pin names not known; wires that end beside it: rom_2_p1, DISP2_IN, {MODE, register_20_q}
  _7_Segment_Display u_7_segment_display_1 (
    .g(undriven_8[7]), .f(undriven_8[6]), .a(undriven_8[5]), .b(undriven_8[4]), .e(undriven_7[3]),
    .d(undriven_7[2]), .c(undriven_7[1]), .dp(undriven_7[0]));
  _7_Segment_Display u_7_segment_display_2 (
    .g(undriven_6[7]), .f(undriven_6[6]), .a(undriven_6[5]), .b(undriven_6[4]), .e(undriven_5[3]),
    .d(undriven_5[2]), .c(undriven_5[1]), .dp(undriven_5[0]));
  // ROM #(.addrWidth(10), .dataWidth(32)) rom_3: pin names not known; wires that end beside it: rom_3_p1, DISP_IN, {MODE2, register_21_q}
  _7_Segment_Display u_7_segment_display_3 (
    .g(undriven_16[7]), .f(undriven_16[6]), .a(undriven_16[5]), .b(undriven_16[4]), .e(undriven_15[3]),
    .d(undriven_15[2]), .c(undriven_15[1]), .dp(undriven_15[0]));
  Decoder #(.select(4)) decoder_9 (
    .out0(decoder_9_out0), .out1(decoder_9_out1), .out2(decoder_9_out2), .out3(decoder_9_out3),
    .out4(decoder_9_out4), .out5(decoder_9_out5), .out6(decoder_9_out6), .out7(decoder_9_out7),
    .sel(counter_9_q[3:0]), .en(PORTB_IN));  // open: out8, out9, out10, out11, out12, out13, out14, out15
  _7_Segment_Display u_7_segment_display_4 (
    .g(undriven_4[7]), .f(undriven_4[6]), .a(undriven_4[5]), .b(undriven_4[4]), .e(undriven_3[3]),
    .d(undriven_3[2]), .c(undriven_3[1]), .dp(undriven_3[0]));
  _7_Segment_Display u_7_segment_display_5 (
    .g(undriven_14[7]), .f(undriven_14[6]), .a(undriven_14[5]), .b(undriven_14[4]), .e(undriven_13[3]),
    .d(undriven_13[2]), .c(undriven_13[1]), .dp(undriven_13[0]));
  _7_Segment_Display u_7_segment_display_6 (
    .g(undriven_12[7]), .f(undriven_12[6]), .a(undriven_12[5]), .b(undriven_12[4]), .e(undriven_11[3]),
    .d(undriven_11[2]), .c(undriven_11[1]), .dp(undriven_11[0]));
  Register register_22 (.D(W_BUS), .en(decoder_9_out0), .Q(register_22_q), .clk(CLK), .clr(RESET));
  Register register_23 (.D(W_BUS), .en(decoder_9_out2), .Q(register_23_q), .clk(CLK), .clr(RESET));
  Register register_24 (.D(W_BUS), .en(decoder_9_out4), .Q(register_24_q), .clk(CLK), .clr(RESET));
  Register register_25 (.D(W_BUS), .en(decoder_9_out6), .Q(register_25_q), .clk(CLK), .clr(RESET));
  _7_Segment_Display u_7_segment_display_7 (
    .g(undriven_2[7]), .f(undriven_2[6]), .a(undriven_2[5]), .b(undriven_2[4]), .e(undriven[3]),
    .d(undriven[2]), .c(undriven[1]), .dp(undriven[0]));
  _7_Segment_Display u_7_segment_display_8 (
    .g(undriven_10[7]), .f(undriven_10[6]), .a(undriven_10[5]), .b(undriven_10[4]), .e(undriven_9[3]),
    .d(undriven_9[2]), .c(undriven_9[1]), .dp(undriven_9[0]));
  Register register_26 (.D(W_BUS), .en(decoder_9_out1), .Q(register_26_q), .clk(CLK), .clr(RESET));
  Register register_27 (.D(W_BUS), .en(decoder_9_out3), .Q(register_27_q), .clk(CLK), .clr(RESET));
  Register register_28 (.D(W_BUS), .en(decoder_9_out5), .Q(register_28_q), .clk(CLK), .clr(RESET));
  Register register_29 (.D(W_BUS), .en(decoder_9_out7), .Q(register_29_q), .clk(CLK), .clr(RESET));
  DotMatrix #(.dotshape("circle"), .inputtype("row"), .matrixcols(8), .matrixrows(8)) dotmatrix_1 (
    .row0(register_22_q), .row1(register_26_q), .row2(register_23_q), .row3(register_27_q),
    .row4(register_24_q), .row5(register_28_q), .row6(register_25_q), .row7(register_29_q));

  // Notes on the sheet:
  //   ADDRESS REGISTER
  //   ADDRESS BUS
  //   DATA BUS
  //   contents of rom_1 (hex, n*v repeats v):
  //   12*1 8 10 0 ef 0 42 1a a0 1 f 10 4 80 1d 2 80 12 8 10 1 d 10 0 2 d 10 0 3 d 10 0 4 d 10 0 c d 10 0
  //   13 7d 81 7f 8 10 0 8 20 0 8 30 0 8 40 0 8 50 8 8 60 0 8 70 0 ef 82 55 11 a3 16 94 c 20 ef 0 2 11 a2
  //   15 90 0 14 10 10 30 1 15 40 0 1a 50 1 4 80 6e 2 80 4c 9 d1 9 e6 8 50 8 ef 0 2 11 a6 15 90 0 c 80 1a
  //   80 1 4 80 a8 ef 0 42 11 a6 15 90 0 10 60 1 8 80 3 1b 81 4 80 a0 8 80 0 f 80 2 80 c8 8 80 1 f 80 2 80
  //   c8 ef 0 42 11 a6 15 90 0 10 60 1 8 80 3 1b 81 4 80 a0 8 80 2 1b 81 4 80 a0 8 80 0 f 80 8 10 0 8 70
  //   40 1b 76 4 80 d9 8 50 8 2 80 4c 7d 81 ad 8 10 0 8 20 0 8 30 0 8 40 0 8 50 8 8 60 0 8 70 0 ef 82 55
  //   11 a3 16 94 c 20 ef 0 42 11 a2 15 90 0 14 10 10 30 1 15 40 0 1a 50 1 4 81 13 2 80 f1 9 d1 8 50 8 ef
  //   0 42 11 a6 15 90 0 c 80 1a 80 1 4 81 4b ef 0 2 11 a6 15 90 0 10 60 1 8 80 3 1b 81 4 81 43 8 80 0 f
  //   80 2 81 6b 8 80 1 f 80 2 81 6b ef 0 2 11 a6 15 90 0 10 60 1 8 80 3 1b 81 4 81 43 8 80 2 1b 81 4 81
  //   43 8 80 0 f 80 8 10 0 8 70 40 1b 76 4 81 7c 8 50 8 2 80 f1 2 80 34 8 10 8 8 20 8 ef 0 2 11 44 c 30
  //   10 a0 1 15 90 0 11 43 1a 20 1 4 81 9d 2 81 88 1a 10 1 9 b1 9 c4 4 82 13 8 20 8 2 81 88 8 10 8 8 20 8
  //   ef 0 42 11 44 c 30 10 a0 1 15 90 0 11 43 1a 20 1 4 81 cb 2 81 b6 1a 10 1 9 b1 9 c4 4 82 13 8 20 8 2
  //   81 b6 8 10 41 ef 0 2 1a 10 1 9 d1 4 82 13 7d 82 14 a 20 0 1 1a 20 e3 3 82 4 8 30 0 f 30 10 a0 1 15
  //   90 0 2 81 e1 8 30 1 f 30 10 a0 1 15 90 0 2 81 e1 5 5 31 10 31 20 31 30 31 40 a 10 0 0 a 30 0 1 9 41
  //   2e 10 2f 10 29 10 80 9 23 2e 30 2f 30 29 30 80 11 32 15 30 13 2e 20 29 20 7f 16 41 16 42 d 30 0 1 d
  //   40 0 0 32 40 32 30 32 20 32 10 5 f 8 9 7 1 3f 38 39 8 9 a 0 2 38 39 3a 9 a b 1 3 39 3a 3b a b c 2 4
  //   3a 3b 3c b c d 3 5 3b 3c 3d c d e 4 6 3c 3d 3e d e f 5 7 3d 3e 3f e f 8 6 0 3e 3f 38 17 10 11 f 9 7
  //   0 1 10 11 12 8 a 0 1 2 11 12 13 9 b 1 2 3 12 13 14 a c 2 3 4 13 14 15 b d 3 4 5 14 15 16 c e 4 5 6
  //   15 16 17 d f 5 6 7 16 17 10 e 8 6 7 0 1f 18 19 17 11 f 8 9 18 19 1a 10 12 8 9 a 19 1a 1b 11 13 9 a b
  //   1a 1b 1c 12 14 a b c 1b 1c 1d 13 15 b c d 1c 1d 1e 14 16 c d e 1d 1e 1f 15 17 d e f 1e 1f 18 16 10 e
  //   f 8 27 20 21 1f 19 17 10 11 20 21 22 18 1a 10 11 12 21 22 23 19 1b 11 12 13 22 23 24 1a 1c 12 13 14
  //   23 24 25 1b 1d 13 14 15 24 25 26 1c 1e 14 15 16 25 26 27 1d 1f 15 16 17 26 27 20 1e 18 16 17 10 2f
  //   28 29 27 21 1f 18 19 28 29 2a 20 22 18 19 1a 29 2a 2b 21 23 19 1a 1b 2a 2b 2c 22 24 1a 1b 1c 2b 2c
  //   2d 23 25 1b 1c 1d 2c 2d 2e 24 26 1c 1d 1e 2d 2e 2f 25 27 1d 1e 1f 2e 2f 28 26 20 1e 1f 18 37 30 31
  //   2f 29 27 20 21 30 31 32 28 2a 20 21 22 31 32 33 29 2b 21 22 23 32 33 34 2a 2c 22 23 24 33 34 35 2b
  //   2d 23 24 25 34 35 36 2c 2e 24 25 26 35 36 37 2d 2f 25 26 27 36 37 30 2e 28 26 27 20 3f 38 39 37 31
  //   2f 28 29 38 39 3a 30 32 28 29 2a 39 3a 3b 31 33 29 2a 2b 3a 3b 3c 32 34 2a 2b 2c 3b 3c 3d 33 35 2b
  //   2c 2d 3c 3d 3e 34 36 2c 2d 2e 3d 3e 3f 35 37 2d 2e 2f 3e 3f 38 36 30 2e 2f 28 7 0 1 3f 39 37 30 31 0
  //   1 2 38 3a 30 31 32 1 2 3 39 3b 31 32 33 2 3 4 3a 3c 32 33 34 3 4 5 3b 3d 33 34 35 4 5 6 3c 3e 34 35
  //   36 5 6 7 3d 3f 35 36 37 6 7 0 3e 38 36 37 30
  //   JUMP LOGIC
  //   32K ROM
  //   PROGRAM COUNTER
  //   32K RAM
  //   INSTRUCTION REGISTER
  //   INSTRUCTION REGISTER 2
  //   OP REG
  //   A REG
  //   B REG
  //   C REG
  //   D REG
  //   E REG
  //   F REG
  //   G REG
  //   H REG
  //   T STATE
  //   contents of _4x28C16 (hex, n*v repeats v):
  //   compressed eJztmM2SgyAMgO95Cs97ikoRH4e16/s/woYftdUASjs725n0ADjk7wsaoAbRaMRGUY/U6y8ahaGJ
  //   U9MyYObMgBqoGRq9TCleqvFSqsd2JwWMFGKXsnWLz67vnfP+yXl6sOKMB5w1hMlmUDXOZE3FMA4C
  //   4AUmahMCwcIjpQreTwS9Lc8cf09WwduaTrq1aFpUqxPG/0m3wdYdFWTcto1FN0mpcbn7ZjCBV+5c
  //   nPXqGzJn5qhUgiXQxQqkgzkmcUvEUKsdM1Gjn6aCDHAxF4QDFnV+YbI01epbzYnrmjCTZoETmOUp
  //   qNK6uBCPX9HEctZ9vm9Pii9DMdCfq+v65xm1VLieYkyU86EsmAsjFElt3ValuNp8833cVzp+X3np
  //   Jf3Mt164hEu4hEu4hOttB5T12EhC+0sof1XdX0L5q6op2gKylZQqhBwM0NPojhDUm35WuQvvovzy
  //   RXnnE7yuugwhL6hwCZdwCZdwCZdwCZdwCdd/4KJmDMd+jZb7d1KS/BFc8AvmcQFd
  //   MICROCODE
  //   INSTRUCTION DECODER ROM (4x2Kx8)
  //   STACK POINTER
  //   ALU REG
  //   FLAGS
  //   FRAME POINTER
  //   OFFSET REGISTER
  //   contents of rom_2 (hex, n*v repeats v):
  //   compressed eJztmE1u7LoOhOdehZdw3AQYezndUnH/S3giP/EAmQQBzuQN7qT1Y5HFKtJ0oi+d1+v8jPPj53yd
  //   8lM67XWEznitR1/5/MrZOrN+fP3MXMqP9ZNPLZeRs0hPy+Izymd6HR8/PmPmcvleP/nUchk5SwtP
  //   C79ex8crjoXx8bTwtPC08LTwtPB4HTOjmhnVzKjmq2KfuVTOlE8tz0XOImktCy2M9bMslBjy4rt4
  //   KDGUGEqM9bNmSgulhdJCi4eUFiqN0kJpobTQsrCMylZUh2VUllFZRmUZlb1KV8tl5CxS42URiRGJ
  //   sX58/cxcKmfKp5WLzEZiRGJEMo/EiMSIxIjMRyRGJEa8Kn87g5XDL12sKo9fySeHyaacgZPGZrAq
  //   L38rYfHLn/Ky62FXRNYEAyeNzWAVaVfVkcOuKGpqlJeqkhzESpw07IJVxVIVkwNefFcmXhwvXvVZ
  //   1ZODsYkXLy8TRpPqnjDKWjpymGyKehcnjc1gFbwG5SVrK98HYhGxyPebIlbipLEZrEoXkSORI5Gj
  //   rLka8EKORI6y9soOL+TIYGQwMhgZOTIYGe+t9ZtrbAar4E0uL0EsQSxBvQSxBLEEsYR2B6AHEEsQ
  //   S1AvQSxBLEEsgbpBLLH7SHeSpUtWS3WTqt0cqqNk7dYw2RQrcdKwC1bVkap2c7hYlZeq3Rwmm8o+
  //   VbWbg7EZrIJuVl7+9ja6G/1td7jd43aX231udzp63aDbDfrdoOMNet6g6w363qDzDXrfoPuN6n+J
  //   Vl4mjCaMJowmjKp2a+CkYResgoZcXqov5lBeRCzy3bOXLl//fSP++0b8n38j7j/7K8Fk+WWi3lkW
  //   TGY/+vTOQmBytZ8vrKpa96R3rHfUO9tzMWSydNuTsXeufrQ9l2J70jvWO+od4acywGTHXBlicvWj
  //   8vznTxBzTXqn9MmJeqdizsnsw5/eKc85ufpRe14xH3vSO7bPqD2rPas9qz2rPetqP9uzdczWMdvL
  //   eke9sz1bx2zoXJOxd65+tD1L27M6ZnXM6piFzjmZ/WjHrI5ZuvpRe/b27O3Zt87VK/Zk+/H27O3Z
  //   27O3Z9+esxsde9I7O+bZasxWY7YaszM4W43sftvP9vzpmD8dc3VNJuqd7fnTMWe3PfZk7J2rH7Xn
  //   0Z5Hex7tebTnsXXe72BOdsz7HcxJex7b89W1cbUaV9fz1WpcrcbValytxtVqXF0bV6uRpX3sSe/s
  //   mDPPPfE9mf3o0zvbc7o88v378+fM97GGz2DwGiabYiVO2to88v2vVXAk3jUMNh0vDyux0gKtvrxW
  //   yaqGwkvWNUw2xUqcLLxUsVbBkcK7XoNNx8vDSqwKL/OxVpmfGgov81fDZFOsxMnCy3qoVXCk8D5j
  //   sOl4eViJFXgOnoPn4Dl4Dp6D5+A5eA6eg+fgOXgOnoPn4HnhTfSc6DnRc6LnRM+JnhM9J3pO9Jzo
  //   OdFzoudEz4meEz0negp+gp/gJ/gJfoKf4Cf4CX6Cn+An+Al+gp/gJ/iJ+hT1KepT1KeoT1Gfoj5F
  //   fYr6FPUp6lPUp6hPUZ+iPkV9Gnoaehp6Gnoaehp6Gnoaehp6Gnoaehp6Gnoaehp6GnoG/AJ+Ab+A
  //   X8Av4BfwC/gF/AJ+Ab+AX8Av4BfwC/gF/AJ+Ab+AX8Av4BfwC/gF/AJ+Ab+AX8Av4Bfwi83vDd4b
  //   vDd4b/De4L3Be4P3Bu8N3hu8N3hv8N7gvcF7g/cuvIGeAz0Heg70HOg50HOg50DPgZ4DPQd6DvQc
  //   6DnQc6DnQE+nvzj9xekvTn9x+ovTX5z+4vQXp784/cXpL05/cfqL01+c/uL0lwd+D/we+D3we+D3
  //   wO+B3wO/B34P/B74PfB74PfA74HfAz/BT/AT/AQ/wU/wE/wEP8FP8BP8BD/BT/AT/AQ/3eDd4N3g
  //   3eDd4N3g3eDd4N3g3eDd4N3g3eDd4N3g3YWX37/1Xc2f9Z3NYX0da/AaJptiJU5afjfre5xD2dX3
  //   ugavYbIpVuJk2dVfCDmUXf0FUYPXMNkUK3ESO8fOsXPsHDvHzrFz7LzsJnFO4pzEOYlzEuckzkmc
  //   kzgFnsATeAJP4Ak8gSfwhJ5CT6Gn0FPoKfQUego9jTiNOI04jTiNOI04jTiz8x4//A94/vA/4PHt
  //   v77z1//1/ctd4O9u/85vt3/HD/d95w/3fce3G77z1zd8/3Cn98tbvPPbLd4/3JX98nbs/HY7dvxw
  //   H3b+cB92fLsBO399A/YPd16/vOVi4CR26Cn0FHoKPYWe0r6vwg49jTiNOI04jTiNOI047bVvutLO
  //   yZ+TPyd/Tv6c/Dn5c/Ln5M/Jn5M/J39O/pz8Oflz8ufkz8mfkz8nf07+nPw5+XPy5+TP910c+fO/
  //   93HYcSe3b+X2vRz5c/Ln5M/Jn5M/J39O/pz8Oflz8ufkz8mfkz9X3wFyCwge+XPy5+TPyZ+TPyd/
  //   Tv6c/Dn5c/Ln5M/Jn5M/J39O/pz8eeXvfzQ8BsM=
  //   contents of rom_3 (hex, n*v repeats v):
  //   compressed eJztmE1u7LoOhOdehZdw3AQYezndUnH/S3giP/EAmQQBzuQN7qT1Y5HFKtJ0oi+d1+v8jPPj53yd
  //   8lM67XWEznitR1/5/MrZOrN+fP3MXMqP9ZNPLZeRs0hPy+Izymd6HR8/PmPmcvleP/nUchk5SwtP
  //   C79ex8crjoXx8bTwtPC08LTwtPB4HTOjmhnVzKjmq2KfuVTOlE8tz0XOImktCy2M9bMslBjy4rt4
  //   KDGUGEqM9bNmSgulhdJCi4eUFiqN0kJpobTQsrCMylZUh2VUllFZRmUZlb1KV8tl5CxS42URiRGJ
  //   sX58/cxcKmfKp5WLzEZiRGJEMo/EiMSIxIjMRyRGJEa8Kn87g5XDL12sKo9fySeHyaacgZPGZrAq
  //   L38rYfHLn/Ky62FXRNYEAyeNzWAVaVfVkcOuKGpqlJeqkhzESpw07IJVxVIVkwNefFcmXhwvXvVZ
  //   1ZODsYkXLy8TRpPqnjDKWjpymGyKehcnjc1gFbwG5SVrK98HYhGxyPebIlbipLEZrEoXkSORI5Gj
  //   rLka8EKORI6y9soOL+TIYGQwMhgZOTIYGe+t9ZtrbAar4E0uL0EsQSxBvQSxBLEEsYR2B6AHEEsQ
  //   S1AvQSxBLEEsgbpBLLH7SHeSpUtWS3WTqt0cqqNk7dYw2RQrcdKwC1bVkap2c7hYlZeq3Rwmm8o+
  //   VbWbg7EZrIJuVl7+9ja6G/1td7jd43aX231udzp63aDbDfrdoOMNet6g6w363qDzDXrfoPuN6n+J
  //   Vl4mjCaMJowmjKp2a+CkYResgoZcXqov5lBeRCzy3bOXLl//fSP++0b8n38j7j/7K8Fk+WWi3lkW
  //   TGY/+vTOQmBytZ8vrKpa96R3rHfUO9tzMWSydNuTsXeufrQ9l2J70jvWO+od4acywGTHXBlicvWj
  //   8vznTxBzTXqn9MmJeqdizsnsw5/eKc85ufpRe14xH3vSO7bPqD2rPas9qz2rPetqP9uzdczWMdvL
  //   eke9sz1bx2zoXJOxd65+tD1L27M6ZnXM6piFzjmZ/WjHrI5ZuvpRe/b27O3Zt87VK/Zk+/H27O3Z
  //   27O3Z9+esxsde9I7O+bZasxWY7YaszM4W43sftvP9vzpmD8dc3VNJuqd7fnTMWe3PfZk7J2rH7Xn
  //   0Z5Hex7tebTnsXXe72BOdsz7HcxJex7b89W1cbUaV9fz1WpcrcbValytxtVqXF0bV6uRpX3sSe/s
  //   mDPPPfE9mf3o0zvbc7o88v378+fM97GGz2DwGiabYiVO2to88v2vVXAk3jUMNh0vDyux0gKtvrxW
  //   yaqGwkvWNUw2xUqcLLxUsVbBkcK7XoNNx8vDSqwKL/OxVpmfGgov81fDZFOsxMnCy3qoVXCk8D5j
  //   sOl4eViJFXgOnoPn4Dl4Dp6D5+A5eA6eg+fgOXgOnoPn4HnhTfSc6DnRc6LnRM+JnhM9J3pO9Jzo
  //   OdFzoudEz4meEz0negp+gp/gJ/gJfoKf4Cf4CX6Cn+An+Al+gp/gJ/iJ+hT1KepT1KeoT1Gfoj5F
  //   fYr6FPUp6lPUp6hPUZ+iPkV9Gnoaehp6Gnoaehp6Gnoaehp6Gnoaehp6Gnoaehp6GnoG/AJ+Ab+A
  //   X8Av4BfwC/gF/AJ+Ab+AX8Av4BfwC/gF/AJ+Ab+AX8Av4BfwC/gF/AJ+Ab+AX8Av4Bfwi83vDd4b
  //   vDd4b/De4L3Be4P3Bu8N3hu8N3hv8N7gvcF7g/cuvIGeAz0Heg70HOg50HOg50DPgZ4DPQd6DvQc
  //   6DnQc6DnQE+nvzj9xekvTn9x+ovTX5z+4vQXp784/cXpL05/cfqL01+c/uL0lwd+D/we+D3we+D3
  //   wO+B3wO/B34P/B74PfB74PfA74HfAz/BT/AT/AQ/wU/wE/wEP8FP8BP8BD/BT/AT/AQ/3eDd4N3g
  //   3eDd4N3g3eDd4N3g3eDd4N3g3eDd4N3g3YWX37/1Xc2f9Z3NYX0da/AaJptiJU5afjfre5xD2dX3
  //   ugavYbIpVuJk2dVfCDmUXf0FUYPXMNkUK3ESO8fOsXPsHDvHzrFz7LzsJnFO4pzEOYlzEuckzkmc
  //   kzgFnsATeAJP4Ak8gSfwhJ5CT6Gn0FPoKfQUego9jTiNOI04jTiNOI04jTiz8x4//A94/vA/4PHt
  //   v77z1//1/ctd4O9u/85vt3/HD/d95w/3fce3G77z1zd8/3Cn98tbvPPbLd4/3JX98nbs/HY7dvxw
  //   H3b+cB92fLsBO399A/YPd16/vOVi4CR26Cn0FHoKPYWe0r6vwg49jTiNOI04jTiNOI047bVvutLO
  //   yZ+TPyd/Tv6c/Dn5c/Ln5M/Jn5M/J39O/pz8Oflz8ufkz8mfkz8nf07+nPw5+XPy5+TP910c+fO/
  //   93HYcSe3b+X2vRz5c/Ln5M/Jn5M/J39O/pz8Oflz8ufkz8mfkz9X3wFyCwge+XPy5+TPyZ+TPyd/
  //   Tv6c/Dn5c/Ln5M/Jn5M/J39O/pz8eeXvfzQ8BsM=
  //   DISPLAY DECODER ROM (4x1Kx8)
  //   DISPLAY DECODER ROM (4x1Kx8)
endmodule

module main2 (
);

  wire and_1_out, and_2_out, or_1_out, OSC_out, RESET_out, RUN_STOP_out, STEP_out, t_ff_1_q, undriven,
       undriven_2, undriven_3, undriven_4, undriven_5, undriven_6, undriven_7, undriven_8;

  Button STEP (.out(STEP_out));
  Button RUN_STOP (.out(RUN_STOP_out));
  Button RESET (.out(RESET_out));
  _74HCT173 u_74hct173_1 (
    .Q1(undriven), .Q2(undriven_2), .Q3(undriven_3), .Q4(undriven_4), .CP(or_1_out), .nOE1(or_1_out),
    .nOE2(or_1_out), .MR(or_1_out), .VCC(1'b1), .GND(or_1_out));  // open: D1, D2, D3, D4, nE1, nE2
  T_Flip_Flop #(.enable("true")) t_ff_1 (
    .clk(RUN_STOP_out), .T(1'b1), .Q(t_ff_1_q), .reset(RESET_out), .en(1'b1));  // open: Qn, preset
  Clock OSC (.out(OSC_out));
  _74HCT173 u_74hct173_2 (
    .Q1(undriven_5), .Q2(undriven_6), .Q3(undriven_7), .Q4(undriven_8), .CP(or_1_out), .nOE1(or_1_out),
    .nOE2(or_1_out), .MR(or_1_out), .VCC(1'b1), .GND(or_1_out));  // open: D1, D2, D3, D4, nE1, nE2
  and and_1 (and_1_out, STEP_out, ~t_ff_1_q);  // AND_Gate
  and and_2 (and_2_out, t_ff_1_q, OSC_out);
  or or_1 (or_1_out, and_1_out, and_2_out);
  // also tied to GND on the sheet: or_1_out
endmodule

module a (
  input  PC_IN,
  input  C_JMP,
  input  Z_JMP,
  input  S_JMP,
  input  C,
  input  Z,
  input  S,
  input  FLAG_INV,
  output JMP
);

  wire and_1_out, and_2_out, and_3_out, and_4_out, and_5_out, and_6_out, and_7_out, and_8_out, and_9_out,
       and_10_out, and_11_out, and_12_out, and_13_out, and_14_out, or_1_out, or_2_out, or_4_out;

  and and_1 (and_1_out, PC_IN, ~Z_JMP);  // AND_Gate
  and and_2 (and_2_out, PC_IN, ~Z_JMP);  // AND_Gate
  and and_3 (and_3_out, ~S, FLAG_INV);  // AND_Gate
  and and_4 (and_4_out, and_1_out, ~S_JMP);  // AND_Gate
  and and_5 (and_5_out, and_2_out, and_3_out);
  and and_6 (and_6_out, PC_IN, ~S_JMP);  // AND_Gate
  and and_7 (and_7_out, ~Z, FLAG_INV);  // AND_Gate
  and and_8 (and_8_out, PC_IN, ~Z_JMP);  // AND_Gate
  and and_9 (and_9_out, S, ~FLAG_INV);  // AND_Gate
  and and_10 (and_10_out, PC_IN, ~S_JMP);  // AND_Gate
  and and_11 (and_11_out, Z, ~FLAG_INV);  // AND_Gate
  or or_1 (or_1_out, and_4_out, and_5_out);
  and and_12 (and_12_out, and_6_out, and_7_out);
  and and_13 (and_13_out, and_8_out, and_9_out);
  and and_14 (and_14_out, and_10_out, and_11_out);
  or or_2 (or_2_out, or_1_out, and_12_out);
  or or_3 (JMP, or_2_out, or_4_out);
  or or_4 (or_4_out, and_13_out, and_14_out);
endmodule

module b (
  input  PC_IN,
  input  C_JMP,
  input  Z_JMP,
  input  S_JMP,
  input  C,
  input  Z,
  input  S,
  input  FLAG_INV,
  output JMP
);

  wire and_1_out, and_2_out, and_3_out, and_4_out, and_5_out, and_6_out, and_7_out, and_8_out, and_9_out,
       and_10_out, and_11_out, and_12_out, and_13_out, and_14_out, and_15_out, and_16_out, and_17_out,
       and_18_out, and_19_out, and_20_out, and_21_out, and_22_out, and_23_out, and_24_out, and_25_out,
       and_26_out, and_27_out, and_28_out, and_29_out, and_30_out, and_31_out, and_32_out, and_33_out,
       and_34_out, or_1_out, or_2_out, or_3_out, or_4_out, or_5_out, or_6_out, or_7_out, or_8_out;

  and and_1 (and_1_out, PC_IN, Z_JMP);
  and and_2 (and_2_out, PC_IN, ~C_JMP);  // AND_Gate
  and and_3 (and_3_out, and_2_out, and_4_out);
  and and_4 (and_4_out, ~Z_JMP, ~S_JMP);  // AND_Gate
  and and_5 (and_5_out, PC_IN, S_JMP);
  and and_6 (and_6_out, and_5_out, and_7_out);
  and and_7 (and_7_out, ~S, FLAG_INV);  // AND_Gate
  and and_8 (and_8_out, PC_IN, S_JMP);
  and and_9 (and_9_out, S, ~FLAG_INV);  // AND_Gate
  and and_10 (and_10_out, PC_IN, Z_JMP);
  and and_11 (and_11_out, ~Z, FLAG_INV);  // AND_Gate
  and and_12 (and_12_out, PC_IN, ~C_JMP);  // AND_Gate
  and and_13 (and_13_out, and_12_out, Z_JMP);
  and and_14 (and_14_out, Z, ~FLAG_INV);  // AND_Gate
  and and_15 (and_15_out, and_1_out, S_JMP);
  and and_16 (and_16_out, and_15_out, and_17_out);
  and and_17 (and_17_out, Z, ~S);  // AND_Gate
  and and_18 (and_18_out, PC_IN, C_JMP);
  and and_19 (and_19_out, and_18_out, and_20_out);
  and and_20 (and_20_out, ~C, FLAG_INV);  // AND_Gate
  and and_21 (and_21_out, PC_IN, C_JMP);
  and and_22 (and_22_out, C, ~FLAG_INV);  // AND_Gate
  and and_23 (and_23_out, PC_IN, C_JMP);
  and and_24 (and_24_out, and_23_out, S_JMP);
  and and_25 (and_25_out, ~Z, S);  // AND_Gate
  and and_26 (and_26_out, PC_IN, C_JMP);
  and and_27 (and_27_out, and_26_out, Z_JMP);
  and and_28 (and_28_out, ~S_JMP, C);  // AND_Gate
  or or_1 (or_1_out, and_3_out, and_6_out);
  and and_29 (and_29_out, and_8_out, and_9_out);
  and and_30 (and_30_out, and_10_out, and_11_out);
  and and_31 (and_31_out, and_13_out, and_14_out);
  or or_2 (or_2_out, and_16_out, and_19_out);
  and and_32 (and_32_out, and_21_out, and_22_out);
  and and_33 (and_33_out, and_24_out, and_25_out);
  and and_34 (and_34_out, and_27_out, and_28_out);
  or or_3 (or_3_out, or_1_out, and_29_out);
  or or_4 (or_4_out, and_30_out, and_31_out);
  or or_5 (or_5_out, or_2_out, and_32_out);
  or or_6 (or_6_out, and_33_out, and_34_out);
  or or_7 (or_7_out, or_3_out, or_4_out);
  or or_8 (or_8_out, or_5_out, or_6_out);
  or or_9 (JMP, or_7_out, or_8_out);
endmodule

module _3nor (
  input  a,
  input  b,
  input  c,
  output o
);

  wire and_1_out;

  and and_1 (and_1_out, ~a, ~b);  // AND_Gate
  and and_2 (o, and_1_out, ~c);  // AND_Gate
endmodule

module _74HCT173 (
  input  Q1,
  input  Q2,
  input  Q3,
  input  Q4,
  input  nE1,
  input  nE2,
  input  CP,
  input  nOE1,
  input  nOE2,
  input  MR,
  input  VCC,
  input  GND,
  output D1,
  output D2,
  output D3,
  output D4
);

  wire and_1_out, and_2_out, register_1_q, register_2_q, register_3_q, register_4_q;

  and and_1 (and_1_out, ~nE1, ~nE2);  // AND_Gate
  Register #(.width(1)) register_1 (.D(Q1), .en(and_1_out), .Q(register_1_q), .clk(CP), .clr(MR));
  Register #(.width(1)) register_2 (.D(Q2), .en(and_1_out), .Q(register_2_q), .clk(CP), .clr(MR));
  Register #(.width(1)) register_3 (.D(Q3), .en(and_1_out), .Q(register_3_q), .clk(CP), .clr(MR));
  Register #(.width(1)) register_4 (.D(Q4), .en(and_1_out), .Q(register_4_q), .clk(CP), .clr(MR));
  and and_2 (and_2_out, ~nOE1, ~nOE2, VCC, ~GND);  // AND_Gate
  assign D1 = and_2_out ? register_1_q : 1'bz;  // Controlled_Buffer controlled_buffer_1
  assign D2 = and_2_out ? register_2_q : 1'bz;  // Controlled_Buffer controlled_buffer_2
  assign D3 = and_2_out ? register_3_q : 1'bz;  // Controlled_Buffer controlled_buffer_3
  assign D4 = and_2_out ? register_4_q : 1'bz;  // Controlled_Buffer controlled_buffer_4
endmodule

module x (
  input  i,
  input  clc,
  output o
);

  and and_1 (o, i, ~clc);  // AND_Gate
endmodule

module xxx (
  input  bit7_in1,
  input  bit7_in2,
  output overflow
);

  and and_1 (overflow, bit7_in1, ~bit7_in2);  // AND_Gate
endmodule

module overflow (
  input  bit7_in1,
  input  bit7_in2,
  input  bit7_out,
  output overflow
);

  wire and_1_out, and_2_out;

  and and_1 (and_1_out, ~bit7_in1, ~bit7_in2, bit7_out);  // AND_Gate
  and and_2 (and_2_out, bit7_in1, bit7_in2, ~bit7_out);  // AND_Gate
  or or_1 (overflow, and_1_out, and_2_out);
endmodule

module ov2 (
  input  bit7_in1,
  input  bit7_in2,
  input  bit7_out,
  output overflow
);

  wire and_1_out, and_2_out, and_3_out, and_4_out;

  and and_1 (and_1_out, ~bit7_in1, ~bit7_in2);  // AND_Gate
  and and_2 (and_2_out, bit7_in1, bit7_in2);
  and and_3 (and_3_out, and_1_out, bit7_out);
  and and_4 (and_4_out, and_2_out, ~bit7_out);  // AND_Gate
  or or_1 (overflow, and_3_out, and_4_out);
endmodule

module jj (
  input  bit7_in1,
  input  bit7_in2,
  output overflow
);

  and and_1 (overflow, bit7_in1, ~bit7_in2);  // AND_Gate
endmodule

module xx (
  input  bit7_in1,
  input  bit7_in2,
  output overflow
);

  wire and_1_out, and_2_out;

  and and_1 (and_1_out, ~bit7_in1, ~bit7_in2);  // AND_Gate
  and and_2 (and_2_out, bit7_in1, bit7_in2);
  or or_1 (overflow, and_1_out, and_2_out);
endmodule

module gfgf (
  input  bit7_in1,
  input  bit7_in2,
  output overflow
);

  and and_1 (overflow, bit7_in1, ~bit7_in2);  // AND_Gate
endmodule
